# Fritzing sketch lcd_hello_world (saved by Fritzing 0.9.3b)
breadboards: 1

parts:
  LCD1 = LCD screen
  Part1 = Arduino Uno (Rev3) - ICSP
  R1 = Resistor [tolerance=±5% resistance=220 package=THT]
  U1 = POT [package=pot_mammoth]

nets:
  VSS: LCD1.VSS, LCD1.R/W, LCD1.LED-, Part1.GND
  VDD: LCD1.VDD, Part1.5V, R1.Pin_0
  N1: LCD1.V0, U1.A
  N2: LCD1.RS, Part1.ICSP_MISO, Part1.D12/MISO
  N3: LCD1.E, Part1.D11_PWM/MOSI
  N4: LCD1.DB4, Part1.D5_PWM
  N5: LCD1.DB5, Part1.D4
  N6: LCD1.DB6, Part1.D3_PWM
  N7: LCD1.DB7, Part1.D2
  N8: LCD1.LED+, R1.Pin_1
